# Fritzing sketch 8LEDs (saved by Fritzing 0.8.7b)
breadboards: 1

parts:
  R1 = Resistor [tolerance=±5% resistance=330 package=THT]
  R2 = Resistor [tolerance=±5% resistance=330 package=THT]
  R3 = Resistor [tolerance=±5% resistance=330 package=THT]
  R4 = Resistor [tolerance=±5% resistance=330 package=THT]
  R5 = Resistor [tolerance=±5% resistance=330 package=THT]
  R6 = Resistor [tolerance=±5% resistance=330 package=THT]
  R7 = Resistor [tolerance=±5% resistance=330 package=THT]
  R8 = Resistor [tolerance=±5% resistance=330 package=THT]
  LED5 = smd LED [color="Yellow (585nm)" package="1206 [SMD]"]
  LED3 = smd LED [color="Red (633nm)" package="1206 [SMD]"]
  LED7 = smd LED [color="Green (555nm)" package="1206 [SMD]"]
  LED4 = smd LED [color="Blue (430nm)" package="1206 [SMD]"]
  LED6 = smd LED [color="White (4500K)" package="1206 [SMD]"]
  LED2 = smd LED [color="Green (555nm)" package="1206 [SMD]"]
  LED8 = smd LED [color="Red (633nm)" package="1206 [SMD]"]
  LED1 = smd LED [color="White (4500K)" package="1206 [SMD]"]
  Arduino1 = Arduino Uno (Rev3)

nets:
  N1: R1.Pin_0, LED1.anode
  N2: R1.Pin_1, Arduino1.D9_PWM
  N3: R2.Pin_0, LED2.anode
  N4: R2.Pin_1, Arduino1.D8
  N5: R3.Pin_0, LED3.anode
  N6: R3.Pin_1, Arduino1.D7
  N7: R4.Pin_0, LED4.anode
  N8: R4.Pin_1, Arduino1.D6_PWM
  N9: R5.Pin_0, LED5.anode
  N10: R5.Pin_1, Arduino1.D5_PWM
  N11: R6.Pin_0, LED6.anode
  N12: R6.Pin_1, Arduino1.D4
  N13: R7.Pin_0, LED7.anode
  N14: R7.Pin_1, Arduino1.D3_PWM
  N15: R8.Pin_0, LED8.anode
  N16: R8.Pin_1, Arduino1.D2
  N17: LED5.cathode, LED3.cathode, LED7.cathode, LED4.cathode, LED6.cathode, LED2.cathode, LED8.cathode, LED1.cathode, Arduino1.GND

notes:
  8 LEDS powered by Arduino, to common ground.
